# Fritzing sketch Schematics (saved by Fritzing 0.9.6b)
breadboards: 1

parts:
  Part1 = Arduino Uno (Rev3) - ICSP
  J1 = Basic Servo
  Part2 = HX711 Weighing Sensor Module
  Part3 = 16-Channel 12-bit PWM Servo Driver - I2C [part_number=815]
  Load_Cell2 = Load Cell - Red/white/black/green
  S1 = Round Pushbutton

nets:
  N1: Part1.A5/SCL, Part3.SCL
  VCC: Part1.5V, Part2.VCC, Part3.VCC
  N2: Part1.ICSP_MOSI, Part3.SDA
  GND: Part1.GND, J1.gnd, Part2.GND, Part3.GND, S1.leg0
  N3: Part1.D11_PWM/MOSI, S1.leg1
  N4: Part1.D2, Part2.CK/TX
  N5: Part1.D3_PWM, Part2.DO/RX
  AC/DC converter: Part1.VIN, J1.vcc, Part3.PWRIN
  N6: J1.pulse, Part3.PWM15
  N7: Part2.E+, Load_Cell2.wire1
  N8: Part2.E-, Load_Cell2.wire2
  N9: Part2.A+, Load_Cell2.wire3
  N10: Part2.A-, Load_Cell2.wire4

custom parts:
  16-Channel 12-bit PWM Servo Driver - I2C: You want to make a cool robot, maybe a hexapod walker, or maybe just a piece of art with a lot of moving parts. Or maybe you want to drive a lot of LEDs with precise PWM output. Using only two pins, control 16 free-running PWM outputs! You can even chain up 62 breakouts to control up to 992 PWM outputs.
  Load Cell - Red/white/black/green: A rectangle load cell/weighting pressure Sensor with four wires - Red, white, black, green. Normally corresponding with E+, E-, A+, A- respectively.
